# Fritzing sketch breadboard (saved by Fritzing 0.9.3b)
breadboards: 1

parts:
  Teensy = Teensy 3.1
  MD1 = Motor Driver 1A Dual TB6612FNG
  MD2 = Motor Driver 1A Dual TB6612FNG
  ENC1 = ENCODER-QUADRATURE [package=encoder-16mm-quad]

nets:
  GND: Teensy.GND, MD1.GND, MD2.GND, ENC1.B
  N1: Teensy.D3, MD1.PWMA
  N2: Teensy.D4, MD1.PWMB
  N3: Teensy.D5, ENC1.A
  N4: Teensy.D6, ENC1.C
  N5: Teensy.D7, MD1.AIN2
  N6: Teensy.D8, MD1.AIN1
  N7: Teensy.D9, MD1.BIN2
  N8: Teensy.D10, MD1.BIN1
  N9: Teensy.D11, MD1.STBY
  N10: MD1.VM, MD2.VM
