# Fritzing sketch perfboard-proto (saved by Fritzing 0.9.3b)
stripboards: 5

parts:
  Teensy1 = Teensy 3.6 (Basic)
  Part1 = Motor Driver 1A Dual TB6612FNG
  Part2 = Motor Driver 1A Dual TB6612FNG
  U1 = ENCODER-QUADRATURE [package=encoder-16mm-quad]
  U2 = ENCODER-QUADRATURE [package=encoder-16mm-quad]
  U3 = ENCODER-QUADRATURE [package=encoder-16mm-quad]
  Part3 = Adafruit FXOS8700 + FXAS21002 9 DoF Breakout [part_number="Adafruit #3463"]
  Part4 = Barometric Pressure Sensor - BMP085 Breakout
  JP1 = Header 4 [package=molex-1x4_lock]
  U5 = Voltage Regulator - 3.3V [package="TO220 [THT]"]
  0_33uF = Ceramic Capacitor [capacitance=100nF package="100 mil [THT, multilayer]"]
  0_1uF = Ceramic Capacitor [capacitance=100nF package="100 mil [THT, multilayer]"]
  J1 = Basic Servo
  J2 = Basic Servo
  J3 = Basic Servo

nets:
  GND: Teensy1.GND, Teensy1.GND1, Part1.GND, Part2.GND, U1.B, U2.B, U3.B, Part3.GND, Part4.GND, JP1.3, JP1.4, 0_33uF.1, 0_1uF.0
  N1: Teensy1.D3, Part1.PWMA
  N2: Teensy1.D4, Part1.PWMB
  N3: Teensy1.D5, J1.pulse
  N4: Teensy1.D6, J2.pulse
  N5: Teensy1.D7, J3.pulse
  N6: Teensy1.D8, Part1.AIN2
  N7: Teensy1.D9, Part1.AIN1
  N8: Teensy1.D10, Part1.STBY
  N9: Teensy1.D11, Part1.BIN1
  N10: Teensy1.D12, Part1.BIN2
  N11: Teensy1.A0/D14, Teensy1.A1/D15
  N12: Teensy1.A2/D16, Teensy1.A3/D17
  N13: Teensy1.A4/D18, U3.A
  N14: Teensy1.A5/D19, U3.C
  N15: Teensy1.A6/D20, U2.A
  N16: Teensy1.A7/D21, U2.C
  N17: Teensy1.A8/D22, U1.A
  N18: Teensy1.A9/D23, U1.C
  VCC: Teensy1.3V3, Teensy1.3V3_1, Part1.VCC, Part2.VCC, Part3.VIN, U5.output_voltage
  N19: Teensy1.D24, Part2.AIN2
  N20: Teensy1.D25, Part2.AIN1
  N21: Teensy1.D26, Part2.STBY
  N22: Teensy1.D27, Part2.BIN1
  N23: Teensy1.D28, Part2.BIN2
  N24: Teensy1.D29, Part2.PWMA
  N25: Teensy1.D30, Part2.PWMB
  N26: Teensy1.D31, Part3.AINT2
  N27: Teensy1.D32, Part3.AINT1
  N28: Teensy1.D33, Part3.SCL
  N29: Teensy1.D34, Part3.SDA
  N30: Teensy1.D35, Part3.GINT1
  N31: Teensy1.D36, Part3.GINT2
  N32: Teensy1.D37, Part3.RST
  N33: Teensy1.D38, Teensy1.D39
  N34: Part1.VM, Part2.VM, JP1.1, JP1.2, 0_33uF.0

custom parts:
  Teensy 3.6 (Basic): The Teensy is a complete USB-based microcontoller development system, in a very small footprint, capable of implementing many types of projects. All programming is done via the USB port. No special programmer is needed, only a standard micro-USB cable and a PC or Macintosh with a USB port.
  Adafruit FXOS8700 + FXAS21002 9 DoF Breakout: The NXP Precision 9DoF breakout combines two of the best motion sensors we've tested here at Adafruit: The FXOS8700 3-Axis accelerometer and magnetometer, and the FXAS21002 3-axis gyroscope. These two sensors combine to make a nice 9-DoF kit, that can be used for motion and orientation sensing. In particular, we think this sensor set is ideal for AHRS-based orientation calculations: the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
